// Logisim project counter.circ as structural Verilog: 1 circuit, main circuit main
module main (
  input  in_1,
  input  in_2,
  input  in_3,
  input  in_4
);

  wire and_1_out, and_2_out, clock_1_out, d_ff_1_q, d_ff_2_q, d_ff_3_q, d_ff_4_q, not_1_out, not_2_out,
       not_3_out, not_4_out, not_5_out, not_6_out, xor_1_out, xor_2_out, xor_3_out;

  not not_1 (not_1_out, d_ff_2_q);
  not not_2 (not_2_out, d_ff_1_q);
  not not_3 (not_3_out, d_ff_1_q);
  and and_1 (and_1_out, d_ff_1_q, not_1_out);
  not not_4 (not_4_out, d_ff_1_q);
  not not_5 (not_5_out, d_ff_2_q);
  not not_6 (not_6_out, d_ff_3_q);
  xor xor_1 (xor_1_out, not_3_out, d_ff_2_q);
  xor xor_2 (xor_2_out, and_1_out, d_ff_3_q);
  and and_2 (and_2_out, not_4_out, not_5_out, not_6_out);
  xor xor_3 (xor_3_out, and_2_out, d_ff_4_q);
  Clock clock_1 (.out(clock_1_out));
  D_Flip_Flop d_ff_1 (.clk(clock_1_out), .D(not_2_out), .Q(d_ff_1_q), .reset(in_1));  // open: Qn, preset, en
  D_Flip_Flop d_ff_2 (.clk(clock_1_out), .D(xor_1_out), .Q(d_ff_2_q), .reset(in_2));  // open: Qn, preset, en
  D_Flip_Flop d_ff_3 (.clk(clock_1_out), .D(xor_2_out), .Q(d_ff_3_q), .reset(in_3));  // open: Qn, preset, en
  D_Flip_Flop d_ff_4 (.clk(clock_1_out), .D(xor_3_out), .Q(d_ff_4_q), .reset(in_4));  // open: Qn, preset, en

  // Notes on the sheet:
  //   4 BIT COUNTER down with a reset
  //   Q1
  //   Q2
  //   Q3
  //   Q4
endmodule
